# Fritzing sketch drawbot_wiring (saved by Fritzing 0.9.3b)

parts:
  Right_Controller = EasyDriver_v44
  Left_Motor = Stepper Motor - Bipolar
  Right_Motor = Stepper Motor - Bipolar
  Raspberry_Pi_Zero1 = Raspberry Pi Zero
  U2 = USB_AB [package=usb-ab-micro-smd]
  Left_Controller = EasyDriver_v44
  U1 = USB_AB [package=usb-ab-micro-smd]
  J1 = Power Jack [package=power_jack_pth]
  Part1 = USB Type A Female Breakout Board [part_number=BOB-12700]
  Part2 = USB Type A Female Breakout Board [part_number=BOB-12700]
  J2 = Dagu DGServo 9g header connector (female) [package=THT]
  J5 = Dagu DGServo 9g header (male) [package=THT]
  Servo_Motor_(for_pen_lift) = Basic Servo

nets:
  GND: Right_Controller.GND, Raspberry_Pi_Zero1.GND, Left_Controller.GND, J1.GND, J2.gnd
  N1: Right_Controller.V+, Left_Controller.V+, J1.PWR
  N2: Right_Controller.STEP, Raspberry_Pi_Zero1.GPIO13
  N3: Right_Controller.DIR, Raspberry_Pi_Zero1.GPIO6
  N4: Right_Controller.OUT2A, U2.GND
  N5: Right_Controller.OUT2B, U2.D+
  N6: Right_Controller.OUT1A, U2.D-
  N7: Right_Controller.OUT1B, U2.VBUS
  N8: Left_Motor.A, Part1.VCC
  N9: Left_Motor.C, Part1.D+
  N10: Left_Motor.B, Part1.D-
  N11: Left_Motor.D, Part1.GND
  N12: Right_Motor.A, Part2.VCC
  N13: Right_Motor.C, Part2.D+
  N14: Right_Motor.B, Part2.D-
  N15: Right_Motor.D, Part2.GND
  3V3: Raspberry_Pi_Zero1.3v3, J2.Vcc
  N16: Raspberry_Pi_Zero1.GPIO21, Left_Controller.STEP
  N17: Raspberry_Pi_Zero1.GPIO20, Left_Controller.DIR
  N18: Raspberry_Pi_Zero1.GPIO18, J2.pulse
  N19: Left_Controller.OUT2A, U1.GND
  N20: Left_Controller.OUT2B, U1.D+
  N21: Left_Controller.OUT1A, U1.D-
  N22: Left_Controller.OUT1B, U1.VBUS
  GND_2: J5.gnd, Servo_Motor_(for_pen_lift).gnd
  VCC: J5.Vcc, Servo_Motor_(for_pen_lift).vcc

notes:
  Wiring for motors can vary a lot, so test connections and don't trust this diagram!

custom parts:
  USB Type A Female Breakout Board: USB breakout board for a Type A connector. sparkfun.com
